# Fritzing sketch circuito-cybertruck (saved by Fritzing 1.0.4)
breadboards: 1

parts:
  ESP32_DEVKIT_V1 = DOIT Esp32 DevKit v1 (30 pins long, 11 pins width) [part_number=ESP32S-PIN30]
  LM2596_(_STEP-DOWN)_6V = RioRand LM2596
  MOTORREDUCTOR_A = gear-motor
  SERVOMOTOR = Basic Servo
  SWITCH = SPST Switch [package=r_sw_th]
  L293D = L293D [package=THT]
  LED = LED - 5mm [color="Red (633nm)" current=0.030A package="5 mm [THT]"]
  L7805 = Voltage Regulator [package=to220-igo]
  BATERIAS_PRINCIPALES = Battery [internal_resistance=0.1Ω]
  BMS_2S = 2S-BMS
  RESISTENCIA = Resistor [tolerance=±5% resistance=220 package="0402 [SMD]"]
  R1 = Resistor [tolerance=±5% resistance=5.1k package="0603 [SMD]"]  # not connected
  R2 = Resistor [tolerance=±5% resistance=2k package="0603 [SMD]"]

nets (from the breadboard view):
  N1: ESP32_DEVKIT_V1.D32, R2.Pin_0
  N2: ESP32_DEVKIT_V1.D25, L293D.In_1
  N3: ESP32_DEVKIT_V1.D26, L293D.In_2
  N4: ESP32_DEVKIT_V1.D27, L293D.Enable_1
  N5: ESP32_DEVKIT_V1.D12, RESISTENCIA.Pin_1
  N6: ESP32_DEVKIT_V1.D13, SERVOMOTOR.pulse
  N7: ESP32_DEVKIT_V1.VIN, L293D.+V, L7805.OUT
  N8: LM2596_(_STEP-DOWN)_6V.Pin_1, SWITCH.P, BMS_2S.pin3#3
  N9: LM2596_(_STEP-DOWN)_6V.Pin_2, BMS_2S.pin3#2
  N10: LM2596_(_STEP-DOWN)_6V.Pin_3, SERVOMOTOR.vcc, L293D.+Vmotor
  N11: LM2596_(_STEP-DOWN)_6V.Pin_4, L293D.0V, LED.cathode, L7805.IN
  N12: MOTORREDUCTOR_A.pin_2, L293D.Out_1_(_Controlled_by_Enable_1_)
  N13: BATERIAS_PRINCIPALES.-, BMS_2S.pin2
  N14: BATERIAS_PRINCIPALES.+, BMS_2S.pin1

notes:
  voltaje cable rojo
  8.4v
  Pin A01 y A02 motor A
  CABLE AZUL
  Cable naranja:[Alimentacion para Esp32 y el integrado L293d
  ALIMENTACION :
  Cable rojo : 8.4 voltios.
  Cable rosa : 6 voltios.
  Cable naranja : 5 voltios.
  Cable negro : Tierra comun.
  Divisor de voltaje para medir porcentaje de bateria
  Led rojo conectado
  al pin d12, aviso de
  conexion a bluetooth

custom parts:
  DOIT Esp32 DevKit v1 (30 pins long, 11 pins width): The DOIT Esp32 DevKit v1 is one of the development board created by DOIT to evaluate the ESP-WROOM-32 module. It is based on the ESP32 microcontroller that boasts Wifi, Bluetooth, Ethernet and Low Power support all in a single chip. (vanepp) made breadboard work, adjusted pin numbering and labels and reduced size of schematic and cleaned up pcb. This chip is 30pins long (2 x15) and 11 pins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
  2S-BMS: 2S-BMS LIPO battery charger / protection unit. Note pcb does not match the board as it will likely connect with wires, so pcb is 5 pads suitable for .1in header pins.
